// Logisim project 四位二进制可逆计数器.circ as structural Verilog: 2 circuits, main circuit main
module main (
  input  CPu,
  input  CLR,
  input  CPd,
  output SD,
  output SB,
  output SC,
  output SA
);

  \四位二进制可逆计数器  \u_四位二进制可逆计数器_1  (.QB(SB), .QD(SD), .QC(SC), .QA(SA), .CLR(CLR), .CPd(CPd), .CPu(CPu));
endmodule

module \四位二进制可逆计数器  (
  input  CLR,
  input  CPd,
  input  CPu,
  output QB,
  output QD,
  output QC,
  output QA
);

  wire and_1_out, and_2_out, and_3_out, and_4_out, and_5_out, and_6_out, D1_qn, D2_qn, D3_qn, D4_qn,
       or_1_out, or_2_out, or_3_out, or_4_out;

  or or_1 (or_1_out, and_1_out, and_2_out);
  and and_1 (and_1_out, D3_qn, D2_qn, D1_qn, CPd);
  D_Flip_Flop #(.trigger("falling")) D4 (
    .clk(or_1_out), .D(D4_qn), .Q(QD), .Qn(D4_qn), .reset(CLR));  // open: preset, en
  and and_2 (and_2_out, QC, QB, QA, CPu);
  and and_3 (and_3_out, D2_qn, D1_qn, CPd);
  D_Flip_Flop #(.trigger("falling")) D3 (
    .clk(or_2_out), .D(D3_qn), .Q(QC), .Qn(D3_qn), .reset(CLR));  // open: preset, en
  or or_2 (or_2_out, and_3_out, and_4_out);
  and and_4 (and_4_out, QB, QA, CPu);
  and and_5 (and_5_out, CPd, D1_qn);
  D_Flip_Flop #(.trigger("falling")) D2 (
    .clk(or_3_out), .D(D2_qn), .Q(QB), .Qn(D2_qn), .reset(CLR));  // open: preset, en
  or or_3 (or_3_out, and_5_out, and_6_out);
  and and_6 (and_6_out, CPu, QA);
  D_Flip_Flop #(.trigger("falling")) D1 (
    .clk(or_4_out), .D(D1_qn), .Q(QA), .Qn(D1_qn), .reset(CLR));  // open: preset, en
  or or_4 (or_4_out, CPu, CPd);
endmodule
