// Logisim project 模六十，二十四计数器，电子钟.circ as structural Verilog: 13 circuits, main circuit main
module main (
  input  CPu,
  input  CLR,
  output \_60进位 ,
  output Q1D,
  output Q1C,
  output Q1B,
  output Q1A,
  output Q0D,
  output Q0C,
  output Q0B,
  output Q0A
);

  wire \模十计数器_1_s10进位 ;

  \模十计数器  \u_模十计数器_1  (.QC(Q0C), .QA(Q0A), .CLR(CLR), .\S10进位 (\模十计数器_1_s10进位 ), .CPu(CPu), .QD(Q0D), .QB(Q0B));
  \模六计数器  \u_模六计数器_1  (
    .CLR(CLR), .CPu(\模十计数器_1_s10进位 ), .S6(\_60进位 ), .SA(Q1A), .SC(Q1C), .SB(Q1B), .SD(Q1D), .in_3(1'b0));
endmodule

module \模十计数器  (
  input  CLR,
  input  CPu,
  output QB,
  output QD,
  output QC,
  output QA,
  output \S10进位 
);

  wire and_1_out, and_2_out, and_3_out, and_4_out, and_5_out, and_6_out, D1_qn, D2_qn, D3_qn, D4_qn,
       or_1_out, or_2_out, or_3_out, or_4_out, or_5_out;

  or or_1 (or_1_out, and_1_out, and_2_out);
  and and_1 (and_1_out, D3_qn, D2_qn, D1_qn, 1'b0);
  and and_2 (and_2_out, QC, QB, QA, CPu);
  D_Flip_Flop #(.trigger("falling")) D4 (
    .clk(or_1_out), .D(D4_qn), .Q(QD), .Qn(D4_qn), .reset(or_5_out));  // open: preset, en
  D_Flip_Flop #(.trigger("falling")) D3 (
    .clk(or_2_out), .D(D3_qn), .Q(QC), .Qn(D3_qn), .reset(or_5_out));  // open: preset, en
  or or_2 (or_2_out, and_3_out, and_4_out);
  and and_3 (and_3_out, D2_qn, D1_qn, 1'b0);
  and and_4 (and_4_out, QB, QA, CPu);
  D_Flip_Flop #(.trigger("falling")) D2 (
    .clk(or_3_out), .D(D2_qn), .Q(QB), .Qn(D2_qn), .reset(or_5_out));  // open: preset, en
  or or_3 (or_3_out, and_5_out, and_6_out);
  and and_5 (and_5_out, 1'b0, D1_qn);
  and and_6 (and_6_out, CPu, QA);
  and and_7 (\S10进位 , QD, QB);
  D_Flip_Flop #(.trigger("falling")) D1 (
    .clk(or_4_out), .D(D1_qn), .Q(QA), .Qn(D1_qn), .reset(or_5_out));  // open: preset, en
  or or_4 (or_4_out, CPu, 1'b0);
  or or_5 (or_5_out, CLR, \S10进位 );
endmodule

module \模六计数器  (
  input  CLR,
  input  CPu,
  input  in_3,
  output S6,
  output SB,
  output SD,
  output SC,
  output SA
);

  wire or_1_out;

  or or_1 (or_1_out, S6, CLR);
  \四位二进制可逆计数器_main  main_1 (.CPu(CPu), .CLR(or_1_out), .CPd(in_3), .SD(SD), .SC(SC), .SB(SB), .SA(SA));
  and and_1 (S6, SC, SB);
endmodule

module \模十计数器封装  (
  input  CPu,
  input  CLR,
  output \S10进位 ,
  output QD,
  output QC,
  output QB,
  output QA
);

  \模十计数器  \u_模十计数器_1  (.QC(QC), .QA(QA), .CLR(CLR), .\S10进位 (\S10进位 ), .CPu(CPu), .QD(QD), .QB(QB));
endmodule

module \六十进制计数器封装  (
  input  CPu,
  input  CLR,
  output Q1D,
  output Q1C,
  output Q1B,
  output Q1A,
  output Q0D,
  output Q0C,
  output Q0B,
  output Q0A,
  output Qcc
);

  main main_1 (
    .CPu(CPu), .CLR(CLR), .Q1D(Q1D), .Q1C(Q1C), .Q1B(Q1B), .Q1A(Q1A), .Q0D(Q0D), .Q0C(Q0C), .Q0B(Q0B),
    .Q0A(Q0A), .\_60进位 (Qcc));
endmodule

module \模二十四计数器  (
  input  CPu,
  input  CLR,
  output Q1D,
  output Q1C,
  output Q1B,
  output Q1A,
  output Q0D,
  output Q0C,
  output Q0B,
  output Q0A,
  output Qcc24
);

  wire and_1_out, or_1_out;

  main main_1 (
    .CPu(CPu), .CLR(or_1_out), .Q1D(Q1D), .Q1C(Q1C), .Q1B(Q1B), .Q1A(Q1A), .Q0D(Q0D), .Q0C(Q0C), .Q0B(Q0B),
    .Q0A(Q0A), .\_60进位 (Qcc24));
  and and_1 (and_1_out, Q1B, Q0C);
  or or_1 (or_1_out, and_1_out, CLR);
endmodule

module \模二十四计数器封装  (
  input  CPu,
  input  CLR,
  output Q1D,
  output Q1C,
  output Q1B,
  output Q1A,
  output Q0D,
  output Q0C,
  output Q0B,
  output Q0A,
  output Qcc
);

  \模二十四计数器  \u_模二十四计数器_1  (
    .CPu(CPu), .Qcc24(Qcc), .CLR(CLR), .Q1D(Q1D), .Q1C(Q1C), .Q1B(Q1B), .Q1A(Q1A), .Q0D(Q0D), .Q0C(Q0C),
    .Q0B(Q0B), .Q0A(Q0A));
endmodule

module \秒计时脉冲产生电路  (
  input  CPu,
  output QCc
);

  \模十计数器  \u_模十计数器_1  (.CLR(QCc), .CPu(CPu), .QD(QCc));  // open: QC, QA, S10进位, QB
endmodule

module \秒计时脉冲产生电路封装  (
  output _1hz
);

  wire _8hz_out;

  Clock _8hz (.out(_8hz_out));
  \秒计时脉冲产生电路  \u_秒计时脉冲产生电路_1  (.CPu(_8hz_out), .QCc(_1hz));
endmodule

module \电子钟  (
  input  CPu,
  input  CLR,
  output [3:0] _240,
  output [3:0] _241,
  output [3:0] _60f0,
  output [3:0] _60f1,
  output [3:0] _60s0,
  output [3:0] _60s1
);

  wire \main_1__60进位 , \main_2__60进位 , \秒计时脉冲产生电路_1_qcc ;

  \模二十四计数器  \u_模二十四计数器_1  (
    .CPu(\main_1__60进位 ), .CLR(CLR), .Q1D(_241[3]), .Q1C(_241[2]), .Q1B(_241[1]), .Q1A(_241[0]),
    .Q0D(_240[3]), .Q0C(_240[2]), .Q0B(_240[1]), .Q0A(_240[0]));  // open: Qcc24
  \秒计时脉冲产生电路  \u_秒计时脉冲产生电路_1  (.CPu(CPu), .QCc(\秒计时脉冲产生电路_1_qcc ));
  main main_1 (
    .CPu(\main_2__60进位 ), .CLR(CLR), .Q1D(_60f1[3]), .Q1C(_60f1[2]), .Q1B(_60f1[1]), .Q1A(_60f1[0]),
    .Q0D(_60f0[3]), .Q0C(_60f0[2]), .Q0B(_60f0[1]), .Q0A(_60f0[0]), .\_60进位 (\main_1__60进位 ));
  main main_2 (
    .CPu(\秒计时脉冲产生电路_1_qcc ), .CLR(CLR), .Q1D(_60s1[3]), .Q1C(_60s1[2]), .Q1B(_60s1[1]), .Q1A(_60s1[0]),
    .Q0D(_60s0[3]), .Q0C(_60s0[2]), .Q0B(_60s0[1]), .Q0A(_60s0[0]), .\_60进位 (\main_2__60进位 ));
endmodule

module \电子钟封装  (
  input  CLR
);

  wire _8hz_out;
  wire [3:0] \电子钟_1__60f0 , \电子钟_1__60f1 , \电子钟_1__60s0 , \电子钟_1__60s1 , \电子钟_1__240 , \电子钟_1__241 ;

  Hex_Digit_Display hex_digit_display_1 (.value(\电子钟_1__241 ));  // open: dp
  Clock _8hz (.out(_8hz_out));
  Hex_Digit_Display hex_digit_display_2 (.value(\电子钟_1__240 ));  // open: dp
  Hex_Digit_Display hex_digit_display_3 (.value(\电子钟_1__60f1 ));  // open: dp
  Hex_Digit_Display hex_digit_display_4 (.value(\电子钟_1__60f0 ));  // open: dp
  \电子钟  \u_电子钟_1  (
    ._241(\电子钟_1__241 ), ._60f1(\电子钟_1__60f1 ), .CPu(_8hz_out), ._60s1(\电子钟_1__60s1 ), ._240(\电子钟_1__240 ),
    ._60f0(\电子钟_1__60f0 ), ._60s0(\电子钟_1__60s0 ), .CLR(CLR));
  Hex_Digit_Display hex_digit_display_5 (.value(\电子钟_1__60s0 ));  // open: dp
  Hex_Digit_Display hex_digit_display_6 (.value(\电子钟_1__60s1 ));  // open: dp
endmodule

module \模六十计数器方便老师检查  (
  input  in_1,
  output out_2,
  output out_3,
  output out_4,
  output out_5,
  output out_6,
  output out_7,
  output out_8,
  output out_9,
  output out_10
);

  wire clock_1_out;

  Clock clock_1 (.out(clock_1_out));
  main main_1 (
    .CPu(clock_1_out), .CLR(in_1), .Q1D(out_2), .Q1C(out_3), .Q1B(out_4), .Q1A(out_5), .Q0D(out_6),
    .Q0C(out_7), .Q0B(out_8), .Q0A(out_9), .\_60进位 (out_10));
endmodule

module \模二十四计数器方便老师检查  (
  input  in_1,
  output out_2,
  output out_3,
  output out_4,
  output out_5,
  output out_6,
  output out_7,
  output out_8,
  output out_9,
  output out_10
);

  wire clock_1_out;

  Clock clock_1 (.out(clock_1_out));
  \模二十四计数器  \u_模二十四计数器_1  (
    .CPu(clock_1_out), .Qcc24(out_10), .CLR(in_1), .Q1D(out_2), .Q1C(out_3), .Q1B(out_4), .Q1A(out_5),
    .Q0D(out_6), .Q0C(out_7), .Q0B(out_8), .Q0A(out_9));
endmodule
