// Logisim project 8421码转化器.circ as structural Verilog: 1 circuit, main circuit main
module main (
  input  A3,
  input  A2,
  input  A1,
  input  A0,
  output S1,
  output S0,
  output S2,
  output S3,
  output S80,
  output S40,
  output S20,
  output S10
);

  wire and_1_out, or_1_out;

  \封装  \u_封装_1  (
    .C4(S10), .A3(A3), .A2(A2), .A1(A1), .A0(A0), .S3(S3), .S2(S2), .S1(S1), .S0(S0), .C0(1'b0), .B0(1'b0),
    .B1(and_1_out), .B2(and_1_out), .B3(1'b0));
  or or_1 (or_1_out, A2, A1);
  and and_1 (and_1_out, A3, or_1_out);

  assign S20 = 1'b0;
  assign S40 = 1'b0;
  assign S80 = 1'b0;
endmodule
