// Logisim project 七段译码器.circ as structural Verilog: 2 circuits, main circuit main
module main (
  input  A3,
  input  A2,
  input  A1,
  input  A0
);

  wire abcdefg_1_a, abcdefg_1_b, abcdefg_1_c, abcdefg_1_d, abcdefg_1_e, abcdefg_1_f, abcdefg_1_g,
       abcdefg_2_a, abcdefg_2_b, abcdefg_2_c, abcdefg_2_d, abcdefg_2_e, abcdefg_2_f, abcdefg_2_g, main_1_s0,
       main_1_s1, main_1_s2, main_1_s3, main_1_s10, main_1_s20, main_1_s40, main_1_s80;

  _7_Segment_Display u_7_segment_display_1 (
    .g(abcdefg_1_g), .f(abcdefg_1_f), .a(abcdefg_1_a), .b(abcdefg_1_b), .e(abcdefg_1_e), .d(abcdefg_1_d),
    .c(abcdefg_1_c));  // open: dp
  abcdefg abcdefg_1 (
    .A0(main_1_s10), .A1(main_1_s20), .A2(main_1_s40), .A3(main_1_s80), .a(abcdefg_1_a), .b(abcdefg_1_b),
    .c(abcdefg_1_c), .d(abcdefg_1_d), .e(abcdefg_1_e), .f(abcdefg_1_f), .g(abcdefg_1_g));
  \_8421码转化器_main  main_1 (
    .A3(A3), .A2(A2), .A1(A1), .A0(A0), .S80(main_1_s80), .S40(main_1_s40), .S20(main_1_s20),
    .S10(main_1_s10), .S3(main_1_s3), .S2(main_1_s2), .S1(main_1_s1), .S0(main_1_s0));
  abcdefg abcdefg_2 (
    .A0(main_1_s0), .A1(main_1_s1), .A2(main_1_s2), .A3(main_1_s3), .a(abcdefg_2_a), .b(abcdefg_2_b),
    .c(abcdefg_2_c), .d(abcdefg_2_d), .e(abcdefg_2_e), .f(abcdefg_2_f), .g(abcdefg_2_g));
  _7_Segment_Display u_7_segment_display_2 (
    .g(abcdefg_2_g), .f(abcdefg_2_f), .a(abcdefg_2_a), .b(abcdefg_2_b), .e(abcdefg_2_e), .d(abcdefg_2_d),
    .c(abcdefg_2_c));  // open: dp
endmodule

module abcdefg (
  input  A0,
  input  A1,
  input  A2,
  input  A3,
  output a,
  output b,
  output c,
  output d,
  output e,
  output f,
  output g
);

  wire and_1_out, and_2_out, and_3_out, and_4_out, and_5_out, and_6_out, and_7_out, and_8_out, and_9_out,
       and_10_out, and_11_out, and_12_out, and_13_out, and_14_out, and_15_out, and_16_out, and_17_out,
       and_18_out, and_19_out, and_20_out, and_21_out, and_22_out, and_23_out, and_24_out, and_25_out,
       not_1_out, not_2_out, not_3_out, not_4_out;

  not not_1 (not_1_out, A0);
  not not_2 (not_2_out, A1);
  not not_3 (not_3_out, A2);
  not not_4 (not_4_out, A3);
  and and_1 (and_1_out, not_3_out, not_2_out, not_1_out);
  and and_2 (and_2_out, A1, not_3_out, not_4_out);
  and and_3 (and_3_out, A0, A2, not_4_out);
  and and_4 (and_4_out, A0, not_2_out, A3);
  or or_1 (a, and_1_out, and_4_out, and_3_out, and_2_out);
  and and_5 (and_5_out, not_4_out, not_3_out);
  and and_6 (and_6_out, not_2_out, not_1_out);
  and and_7 (and_7_out, not_3_out, not_2_out);
  and and_8 (and_8_out, not_4_out, A1, A0);
  and and_9 (and_9_out, not_4_out, A2);
  and and_10 (and_10_out, not_3_out, not_2_out);
  and and_11 (and_11_out, not_3_out, A0);
  and and_12 (and_12_out, A2, not_2_out, A0);
  and and_13 (and_13_out, not_3_out, not_1_out);
  and and_14 (and_14_out, not_3_out, A0, A1);
  and and_15 (and_15_out, not_1_out, A1, A2);
  and and_16 (and_16_out, not_1_out, A1);
  and and_17 (and_17_out, not_1_out, not_3_out);
  and and_18 (and_18_out, not_2_out, not_1_out);
  and and_19 (and_19_out, not_2_out, A2);
  and and_20 (and_20_out, not_2_out, not_3_out, A3);
  and and_21 (and_21_out, A2, not_1_out);
  and and_22 (and_22_out, not_2_out, A2);
  and and_23 (and_23_out, A3, not_3_out);
  and and_24 (and_24_out, not_3_out, A1);
  and and_25 (and_25_out, not_1_out, A1);
  or or_2 (e, and_16_out, and_17_out);
  or or_3 (b, and_5_out, and_6_out, and_7_out, and_8_out);
  or or_4 (c, and_9_out, and_10_out, and_11_out);
  or or_5 (d, and_12_out, and_13_out, and_14_out, and_15_out);
  or or_6 (f, and_18_out, and_19_out, and_20_out, and_21_out);
  or or_7 (g, and_22_out, and_23_out, and_24_out, and_25_out);
endmodule
