// Logisim project 四位二进制串行加法器.circ as structural Verilog: 3 circuits, main circuit main
module main (
  input  A0,
  input  B0,
  input  A1,
  input  C0,
  input  B1,
  input  A2,
  input  B2,
  input  A3,
  input  B3,
  output S0,
  output S1,
  output S2,
  output S3,
  output C4
);

  wire \二进制全加器_1_ci , \二进制全加器_2_ci , \二进制全加器_3_ci ;

  \二进制全加器  \u_二进制全加器_1  (.A(A0), .B(B0), .C(C0), .S(S0), .Ci(\二进制全加器_1_ci ));
  \二进制全加器  \u_二进制全加器_2  (.A(A1), .B(B1), .C(\二进制全加器_1_ci ), .S(S1), .Ci(\二进制全加器_2_ci ));
  \二进制全加器  \u_二进制全加器_3  (.A(A2), .B(B2), .C(\二进制全加器_2_ci ), .S(S2), .Ci(\二进制全加器_3_ci ));
  \二进制全加器  \u_二进制全加器_4  (.A(A3), .B(B3), .C(\二进制全加器_3_ci ), .S(S3), .Ci(C4));
endmodule

module \二进制全加器  (
  input  A,
  input  B,
  input  C,
  output S,
  output Ci
);

  wire nand_1_out, nand_2_out, nand_3_out, nand_4_out, nand_5_out, nand_6_out, nand_7_out, nand_8_out,
       nand_9_out, nand_10_out, nand_11_out, nand_12_out, nand_13_out;

  nand nand_1 (nand_1_out, A, A);
  nand nand_2 (nand_2_out, B, B);
  nand nand_3 (nand_3_out, A, A);
  nand nand_4 (nand_4_out, C, C);
  nand nand_5 (nand_5_out, B, B);
  nand nand_6 (nand_6_out, C, C);
  nand nand_7 (nand_7_out, B, C);
  nand nand_8 (nand_8_out, A, C);
  nand nand_9 (nand_9_out, A, B);
  nand nand_10 (nand_10_out, nand_1_out, nand_2_out, C);
  nand nand_11 (nand_11_out, nand_3_out, B, nand_4_out);
  nand nand_12 (nand_12_out, A, nand_5_out, nand_6_out);
  nand nand_13 (nand_13_out, A, B, C);
  nand nand_14 (Ci, nand_7_out, nand_8_out, nand_9_out);
  nand nand_15 (S, nand_10_out, nand_11_out, nand_12_out, nand_13_out);
endmodule

module \封装  (
  input  C0,
  input  B0,
  input  A3,
  input  B1,
  input  A2,
  input  B2,
  input  A1,
  input  B3,
  input  A0,
  output S1,
  output S0,
  output S2,
  output S3,
  output C4
);

  main main_1 (
    .A0(A0), .B0(B0), .A1(A1), .C0(C0), .B1(B1), .A2(A2), .B2(B2), .A3(A3), .B3(B3), .S0(S0), .S1(S1),
    .S2(S2), .S3(S3), .C4(C4));
endmodule
