// Logisim project 满员时系统提示.circ as structural Verilog: 2 circuits, main circuit main
module main (
  input  CPu,
  input  CLR,
  input  CPd,
  output e,
  output f,
  output g,
  output a,
  output b,
  output c,
  output d,
  output e_2,
  output f_2,
  output g_2,
  output a_2,
  output b_2,
  output c_2,
  output d_2,
  output \警告 
);

  wire and_2_out, and_3_out, and_4_out, main_1_s0, main_1_s1, main_1_s2, main_1_s3, main_1_s10, main_1_s20,
       main_1_s40, main_1_s80, main_2_sa, main_2_sb, main_2_sc, main_2_sd, not_1_out, or_1_out;

  abcdefg abcdefg_1 (
    .A0(main_1_s10), .A1(main_1_s20), .A2(main_1_s40), .A3(main_1_s80), .a(a_2), .b(b_2), .c(c_2), .d(d_2),
    .e(e_2), .f(f_2), .g(g_2));
  and and_1 (\警告 , CPu, and_2_out);
  or or_1 (or_1_out, main_2_sd, main_2_sb, main_2_sa, main_2_sc);
  not not_1 (not_1_out, and_2_out);
  abcdefg abcdefg_2 (
    .A0(main_1_s0), .A1(main_1_s1), .A2(main_1_s2), .A3(main_1_s3), .a(a), .b(b), .c(c), .d(d), .e(e), .f(f),
    .g(g));
  and and_2 (and_2_out, main_2_sd, main_2_sb, main_2_sc, main_2_sa);
  and and_3 (and_3_out, not_1_out, CPu);
  and and_4 (and_4_out, or_1_out, CPd);
  \_8421码转化器_main  main_1 (
    .A3(main_2_sd), .A2(main_2_sc), .A1(main_2_sb), .A0(main_2_sa), .S80(main_1_s80), .S40(main_1_s40),
    .S20(main_1_s20), .S10(main_1_s10), .S3(main_1_s3), .S2(main_1_s2), .S1(main_1_s1), .S0(main_1_s0));
  \四位二进制可逆计数器_main  main_2 (
    .CPu(and_3_out), .CLR(CLR), .CPd(and_4_out), .SD(main_2_sd), .SC(main_2_sc), .SB(main_2_sb),
    .SA(main_2_sa));
endmodule

module \验证全系统  (
  input  CPu,
  input  CLR,
  input  CPd,
  output \报警 
);

  wire main_1_a, main_1_a_2, main_1_b, main_1_b_2, main_1_c, main_1_c_2, main_1_d, main_1_d_2, main_1_e,
       main_1_e_2, main_1_f, main_1_f_2, main_1_g, main_1_g_2;

  _7_Segment_Display u_7_segment_display_1 (
    .g(main_1_g_2), .f(main_1_f_2), .a(main_1_a_2), .b(main_1_b_2), .e(main_1_e_2), .d(main_1_d_2),
    .c(main_1_c_2));  // open: dp
  main main_1 (
    .CPu(CPu), .CLR(CLR), .CPd(CPd), .a_2(main_1_a_2), .b_2(main_1_b_2), .c_2(main_1_c_2), .\警告 (\报警 ),
    .d_2(main_1_d_2), .e_2(main_1_e_2), .f_2(main_1_f_2), .g_2(main_1_g_2), .a(main_1_a), .b(main_1_b),
    .c(main_1_c), .d(main_1_d), .e(main_1_e), .f(main_1_f), .g(main_1_g));
  _7_Segment_Display u_7_segment_display_2 (
    .g(main_1_g), .f(main_1_f), .a(main_1_a), .b(main_1_b), .e(main_1_e), .d(main_1_d), .c(main_1_c));  // open: dp
endmodule
